# Fritzing sketch 230V Remote (saved by Fritzing 0.8.7b)
circuit board: 4cm x 6cm
breadboards: 1

parts:
  Part1 = Arduino Nano (Rev3.0)
  J3 = female pin header, 3 pins [form="♀ (female)"]
  J2 = female pin header, 2 pins [form="♀ (female)"]
  J4 = female pin header, 2 pins [form="♀ (female)"]

nets:
  N1: Part1.GND, J3.pin3, J4.pin1, J4.pin2
  N2: Part1.D2, J3.pin1
  N3: Part1.D3, J2.pin2
  N4: Part1.D4, J2.pin1
  N5: Part1.5V, J3.pin2
